# Fritzing sketch lab1a-topology (saved by Fritzing 0.9.3b)

parts:
  Part1 = SunFounder HAT for Picar
  Raspberry_Pi_1 = Raspberry Pi 3 [part_number=RPI-3-V1.2]
  VCC1 = Battery
  HC-SR04_Sensor_1 = HC-SR04 Ultrasonic Distance Sensor
  J1 = Basic Servo
  M1 = DC Motor
  IC1 = Rasberry Pi NIOR Camera [chip_label=IC package="DIP (Dual Inline) [THT]"]  # not connected
  M2 = DC Motor
  M3 = DC Motor
  M4 = DC Motor

nets:
  N1: Part1.B6, M1.pin_1, M4.pin_2
  N2: Part1.B5, M1.pin_2, M4.pin_1
  N3: Part1.B4, HC-SR04_Sensor_1.GND, M2.pin_2
  N4: Part1.B3, HC-SR04_Sensor_1.ECHO, M2.pin_1
  N5: Part1.B2, HC-SR04_Sensor_1.TRIG, M3.pin_2
  N6: Part1.B1, HC-SR04_Sensor_1.VCC, M3.pin_1
  N7: Part1.A4, VCC1.+
  N8: Part1.A5, VCC1.-
  N9: Part1.A6, Raspberry_Pi_1.ID_SD
  N10: Part1.N$9, J1.gnd
  N11: Part1.N$12, J1.vcc
  N12: Part1.N$16, J1.pulse
  N13: Part1.N$47, Raspberry_Pi_1.GPIO21
  N14: Part1.N$48, Part1.N$54, Part1.pin_81, Part1.pin_85, Part1.pin_91, Part1.pin_94, Part1.pin_99, Part1.pin_105, Raspberry_Pi_1.GND
  N15: Part1.N$49, Raspberry_Pi_1.GPIO26
  N16: Part1.N$50, Raspberry_Pi_1.GPIO20
  N17: Part1.N$51, Raspberry_Pi_1.GPIO19
  N18: Part1.N$52, Raspberry_Pi_1.GPIO16
  N19: Part1.N$53, Raspberry_Pi_1.GPIO13
  N20: Part1.N$55, Raspberry_Pi_1.GPIO6
  N21: Part1.N$57, Raspberry_Pi_1.GPIO12
  N22: Part1.N$63, Raspberry_Pi_1.GPIO7
  N23: Part1.N$64, Raspberry_Pi_1.GPIO11
  N24: Part1.pin_80, Raspberry_Pi_1.GPIO8
  N25: Part1.pin_82, Raspberry_Pi_1.GPIO9
  N26: Part1.pin_83, Raspberry_Pi_1.GPIO25
  N27: Part1.pin_84, Raspberry_Pi_1.GPIO10
  3V3: Part1.pin_86, Part1.pin_102, Raspberry_Pi_1.3v3, Raspberry_Pi_1.3V3
  N28: Part1.pin_87, Raspberry_Pi_1.GPIO24
  N29: Part1.pin_88, Raspberry_Pi_1.GPIO22
  N30: Part1.pin_89, Raspberry_Pi_1.GPIO23
  N31: Part1.pin_90, Raspberry_Pi_1.GPIO27
  N32: Part1.pin_92, Raspberry_Pi_1.GPIO17
  N33: Part1.pin_93, Raspberry_Pi_1.GPIO18
  N34: Part1.pin_95, Raspberry_Pi_1.GPIO15
  N35: Part1.pin_96, Raspberry_Pi_1.GPIO4
  N36: Part1.pin_97, Raspberry_Pi_1.GPIO14
  N37: Part1.pin_98, Raspberry_Pi_1.GPIO3
  N38: Part1.pin_100, Raspberry_Pi_1.GPIO2
  N39: Part1.pin_101, Part1.pin_103, Raspberry_Pi_1.5V
  N40: Part1.pin_104, Raspberry_Pi_1.GPIO5
  N41: Part1.pin_106, Raspberry_Pi_1.ID_SC

notes:
  Raspberry Pi connected to 4WD hat via 20 pin connector
  Grayscale Sensor
  Ultrasonic Sensor
  18650 Battery Pack
  Servor Arm Motor
  Photo-interrupter Sensor
  Raspberry Pi Camera Module 2
  connected via ribbon cable
  Motor 1
  Motor 2
  Motor 3
  Motor 4

custom parts:
  Rasberry Pi NIOR Camera: Camera
